# Fritzing sketch hardware-platform (saved by Fritzing 0.8.3b)
breadboards: 1

parts:
  IC3 = IC, DIP package, 40 pins [chip_label=1284p]
  IC2 = IC, DIP package, 16 pins [chip_label=232]
  LED2 = LED - 5mm [color="Red (660nm)" package="5 mm [THT]"]
  R1 = Resistor [tolerance=±5% resistance=220 package=THT]
  C1 = Ceramic Capacitor [capacitance=100nF package="100 mil [THT, multilayer]"]
  C2 = Ceramic Capacitor [capacitance=100nF package="100 mil [THT, multilayer]"]
  C3 = Ceramic Capacitor [capacitance=100nF package="100 mil [THT, multilayer]"]
  C4 = Ceramic Capacitor [capacitance=100nF package="100 mil [THT, multilayer]"]
  DB9 = DB9 Connector [package=db9]
  U1 = XBee
  JTAG1 = shrouded pin header, 10 pins [form="♂ (shrouded male)"]
  LED3 = LED - 5mm [color="Yellow (595nm)" package="5 mm [THT]"]
  LED4 = LED - 5mm [color="Orange (620nm)" package="5 mm [THT]"]
  TSL252R = Photocell (LDR) [package=THT]

nets:
  RESET: IC3.pin9, JTAG1.pin6
  3.3V: IC3.pin10, IC3.pin30, IC2.pin16, R1.Pin_0, C1.1, U1.VCC, JTAG1.pin4, TSL252R.pin_0
  GND: IC3.pin11, IC3.pin31, IC2.pin15, LED2.anode, C1.0, DB9.5, U1.GND, JTAG1.pin2, JTAG1.pin10, LED3.cathode, LED4.cathode
  RX0: IC3.pin14, U1.pin2
  TX0: IC3.pin15, U1.pin3
  RX1: IC3.pin16, IC2.pin12
  TX1: IC3.pin17, IC2.pin11
  TCK: IC3.pin24, JTAG1.pin1
  TMS: IC3.pin25, JTAG1.pin5
  TDO: IC3.pin26, JTAG1.pin3
  TDI: IC3.pin27, JTAG1.pin9
  N1: IC3.pin40, TSL252R.pin_1
  N2: IC2.pin1, C2.1
  N3: IC2.pin2, C4.1
  N4: IC2.pin3, C2.0
  N5: IC2.pin4, C3.1
  N6: IC2.pin5, C3.0
  N7: IC2.pin6, C4.0
  TX: IC2.pin13, DB9.3
  RX: IC2.pin14, DB9.2
  N8: LED2.cathode, R1.Pin_1
  N9: U1.pin13, LED4.anode
  N10: U1.pin15, LED3.anode
