# Fritzing sketch node-capture-jtag (saved by Fritzing 0.8.3b)
breadboards: 1

parts:
  IC4 = IC, DIP package, 40 pins [chip_label=1284p]
  JTAG = shrouded pin header, 10 pins [form="♂ (shrouded male)"]

nets:
  RESET: IC4.pin9, JTAG.pin6
  TCK: IC4.pin24, JTAG.pin1
  TMS: IC4.pin25, JTAG.pin5
  TDO: IC4.pin26, JTAG.pin3
  TDI: IC4.pin27, JTAG.pin9
  GND: JTAG.pin2, JTAG.pin10
  5V: JTAG.pin4
