# Fritzing sketch node-capture (saved by Fritzing 0.8.3b)
breadboards: 1

parts:
  IC3 = IC, DIP package, 40 pins [chip_label=1284p]
  IC2 = IC, DIP package, 16 pins [chip_label=232]
  LED2 = LED - 5mm [color="Green (555nm)" package="5 mm [THT]"]
  R1 = Resistor [tolerance=±5% resistance=220 package=THT]
  C1 = Ceramic Capacitor [capacitance=100nF package="100 mil [THT, multilayer]"]
  C2 = Ceramic Capacitor [capacitance=100nF package="100 mil [THT, multilayer]"]
  C3 = Ceramic Capacitor [capacitance=100nF package="100 mil [THT, multilayer]"]
  C4 = Ceramic Capacitor [capacitance=100nF package="100 mil [THT, multilayer]"]
  DB9 = DB9 Connector [package=db9]

nets:
  5V: IC3.pin10, IC2.pin16, C1.1
  GND: IC3.pin11, IC2.pin15, R1.Pin_0, C1.0, DB9.5
  N1: IC3.pin14, IC2.pin12
  N2: IC3.pin15, IC2.pin11
  N3: IC3.pin20, LED2.anode
  N4: IC2.pin1, C2.1
  N5: IC2.pin2, C4.1
  N6: IC2.pin3, C2.0
  N7: IC2.pin4, C3.1
  N8: IC2.pin5, C3.0
  N9: IC2.pin6, C4.0
  TX: IC2.pin13, DB9.3
  RX: IC2.pin14, DB9.2
  N10: LED2.cathode, R1.Pin_1
